# Fritzing sketch Send (saved by Fritzing 0.9.3b)
breadboards: 1

parts:
  Part1 = Arduino Nano (Rev3.0)
  RF_RX = mystery part, 3 pins [chip_label="RF TX"]
  BMP180 = Barometric Pressure Sensor - BMP180 Breakout (GY-68)
  DHT11 = DHT11 Humitidy and Temperature Sensor
  R1 = Resistor [tolerance=±5% resistance=4.7k package=THT]
  VCC1 = Battery block 9V

nets:
  GND: Part1.GND, RF_RX.pin3, BMP180.GND, DHT11.GND, VCC1.-
  N1: Part1.D2, DHT11.DATA, R1.Pin_1
  N2: Part1.D12/MISO, RF_RX.pin1
  N3: Part1.VIN, VCC1.+
  5V: Part1.5V, RF_RX.pin2, DHT11.VDD, R1.Pin_0
  N4: Part1.A5, BMP180.SCL
  N5: Part1.A4, BMP180.SDA
  3V3: Part1.3V3, BMP180.VCC

notes:
  Transmitter
  3.3 V rail
  5 V rail
  A4 - SDA
  A5 - SCL

custom parts:
  DHT11 Humitidy and Temperature Sensor: DHT11 Humidity and Temperature Sensor
