# Fritzing sketch Send_perfboard (saved by Fritzing 0.9.3b)
circuit board: 8.46667cm x 5.64444cm
perfboards: 1

parts:
  VCC1 = Battery block 9V
  BMP180 = Barometric Pressure Sensor - BMP180 Breakout (GY-68)
  RF_TX = mystery part, 3 pins [chip_label="RF TX"]
  DHT11 = DHT11 Humitidy and Temperature Sensor
  Part1 = Arduino Nano (Rev3.0) (ICSP)
  R1 = Resistor [tolerance=±5% resistance=4.7k package=THT]

nets:
  GND: VCC1.-, BMP180.GND, RF_TX.pin3, DHT11.GND, Part1.GND
  N1: VCC1.+, Part1.VIN
  VCC: BMP180.VCC, Part1.3V3
  N2: BMP180.SCL, Part1.A5
  N3: BMP180.SDA, Part1.A4
  N4: RF_TX.pin1, Part1.D12/MISO
  VDD: RF_TX.pin2, DHT11.VDD, Part1.5V, R1.Pin_1
  N5: DHT11.DATA, Part1.D2, R1.Pin_0

notes:
  A4 - SDA
  A5 - SCL

custom parts:
  DHT11 Humitidy and Temperature Sensor: DHT11 Humidity and Temperature Sensor
